// Logisim project fulladder.circ as structural Verilog: 1 circuit, main circuit Full-Adder
module Full_Adder (
  input  A,
  input  B,
  input  CARRY,
  output SUM,
  output CARRY_2
);

  wire and_1_out, and_2_out, xor_1_out;

  xor xor_1 (xor_1_out, A, B);
  and and_1 (and_1_out, A, B);
  and and_2 (and_2_out, xor_1_out, CARRY, CARRY);
  xor xor_2 (SUM, xor_1_out, CARRY);
  or or_1 (CARRY_2, and_1_out, and_2_out);
endmodule
