// Logisim project lukas.circ as structural Verilog
module Full_Adder (
  input  A,
  input  B,
  input  CARRY,
  output SUM,
  output CARRY_2
);

  wire and_1_out, and_2_out, xor_1_out;

  xor xor_1 (xor_1_out, A, B);
  and and_1 (and_1_out, A, B);
  and and_2 (and_2_out, xor_1_out, CARRY, CARRY);
  xor xor_2 (SUM, xor_1_out, CARRY);
  or or_1 (CARRY_2, and_1_out, and_2_out);
endmodule

module LK__8_Bit_Adder (
  input  CARRY,
  input  [7:0] A,
  input  [7:0] B,
  output [7:0] SUM,
  output OVERFLOW
);

  wire full_adder_1_carry_2, full_adder_2_carry_2, full_adder_3_carry_2, full_adder_4_carry_2,
       full_adder_5_carry_2, full_adder_6_carry_2, full_adder_7_carry_2;

  Full_Adder full_adder_1 (.A(A[0]), .B(B[0]), .CARRY(CARRY), .SUM(SUM[0]), .CARRY_2(full_adder_1_carry_2));
  Full_Adder full_adder_2 (
    .A(A[1]), .B(B[1]), .CARRY(full_adder_1_carry_2), .SUM(SUM[1]), .CARRY_2(full_adder_2_carry_2));
  Full_Adder full_adder_3 (
    .A(A[2]), .B(B[2]), .CARRY(full_adder_2_carry_2), .SUM(SUM[2]), .CARRY_2(full_adder_3_carry_2));
  Full_Adder full_adder_4 (
    .A(A[3]), .B(B[3]), .CARRY(full_adder_3_carry_2), .SUM(SUM[3]), .CARRY_2(full_adder_4_carry_2));
  Full_Adder full_adder_5 (
    .A(A[4]), .B(B[4]), .CARRY(full_adder_4_carry_2), .SUM(SUM[4]), .CARRY_2(full_adder_5_carry_2));
  Full_Adder full_adder_6 (
    .A(A[5]), .B(B[5]), .CARRY(full_adder_5_carry_2), .SUM(SUM[5]), .CARRY_2(full_adder_6_carry_2));
  Full_Adder full_adder_7 (
    .A(A[6]), .B(B[6]), .CARRY(full_adder_6_carry_2), .SUM(SUM[6]), .CARRY_2(full_adder_7_carry_2));
  Full_Adder full_adder_8 (.A(A[7]), .B(B[7]), .CARRY(full_adder_7_carry_2), .SUM(SUM[7]), .CARRY_2(OVERFLOW));
endmodule

module Incrementor (
  input  [7:0] INPUT,
  output [7:0] OUTPUT,
  output OVERFLOW
);

  LK__8_Bit_Adder lk_8_bit_adder_1 (.CARRY(1'b0), .A(INPUT), .B(8'h1), .SUM(OUTPUT), .OVERFLOW(OVERFLOW));
endmodule

module TTYDecoder (
  input  [3:0] Data,
  input  Clock,
  output [6:0] TTY_Data,
  output TTY_Clock
);

  wire freqdivide2_1_clock__2, not_1_out;
  wire [7:0] lk_8_bit_adder_1_sum;

  DotMatrix #(.matrixcols(1), .matrixrows(4)) dotmatrix_1 (.col0(Data));
  not not_1 (not_1_out, freqdivide2_1_clock__2);
  FreqDivide2 freqdivide2_1 (.Clock(Clock), .Clock__2(freqdivide2_1_clock__2));
  LK__8_Bit_Adder lk_8_bit_adder_1 (
    .CARRY(1'b0), .A({4'b0000, Data}), .B(8'h30), .SUM(lk_8_bit_adder_1_sum));  // open: OVERFLOW
  Multiplexer #(.width(7), .disabled(0), .enable("false")) multiplexer_1 (
    .in0(lk_8_bit_adder_1_sum[6:0]), .in1(7'b0100000), .out(TTY_Data), .sel(not_1_out));

  assign TTY_Clock = Clock;
endmodule

module FreqDivide2 (
  input  Clock,
  output Clock__2
);

  wire d_ff_1_qn;

  D_Flip_Flop d_ff_1 (.clk(Clock), .D(d_ff_1_qn), .Q(Clock__2), .Qn(d_ff_1_qn));  // open: preset, en, reset
endmodule

module TTY_example (
);

  wire Clear_out, clock_1_out, ttydecoder_1_tty_clock;
  wire [3:0] random_1_out;
  wire [6:0] ttydecoder_1_tty_data;

  Clock clock_1 (.out(clock_1_out));
  Random #(.width(4)) random_1 (.clk(clock_1_out), .out(random_1_out));  // open: next, clr
  TTYDecoder ttydecoder_1 (
    .Data(random_1_out), .Clock(clock_1_out), .TTY_Data(ttydecoder_1_tty_data),
    .TTY_Clock(ttydecoder_1_tty_clock));
  TTY tty_1 (.data(ttydecoder_1_tty_data), .clk(ttydecoder_1_tty_clock), .clr(Clear_out));  // open: we
  Button Clear (.out(Clear_out));
endmodule
